// Logisim project connect4_circuit.circ as structural Verilog: 10 circuits, main circuit main
module main (
);

  wire buffer_1_out, buffer_2_out, buffer_3_out, buffer_4_out, buffer_5_out, buffer_6_out, buffer_7_out,
       buffer_8_out, buffer_9_out, button_1_out, button_2_out, button_3_out, button_4_out, button_5_out,
       button_6_out, button_7_out, move_1_valid, nor_1_out, one_tick_pulse_1_x, one_tick_pulse_2_x,
       one_tick_pulse_3_x, one_tick_pulse_4_x, one_tick_pulse_5_x, one_tick_pulse_6_x, one_tick_pulse_7_x,
       or_1_out, R_out, Turn_p;
  wire [2:0] priority_encoder_1_out;
  wire [6:0] state_memory_1_out_3, state_memory_1_out_3_2, state_memory_1_out_3_3, state_memory_1_out_3_4,
       state_memory_1_out_3_5, state_memory_1_out_3_6, state_memory_1_out_3_7;
  wire [48:0] move_1_s_new, multiplexer_1_out, reset_state_1_out_1;

  Button R (.out(R_out));
  column_rgb column_rgb_1 (.C(state_memory_1_out_3_7));
  column_rgb column_rgb_2 (.C(state_memory_1_out_3_6));
  column_rgb column_rgb_3 (.C(state_memory_1_out_3_5));
  column_rgb column_rgb_4 (.C(state_memory_1_out_3_4));
  Button button_1 (.out(button_1_out));
  Button button_2 (.out(button_2_out));
  Button button_3 (.out(button_3_out));
  Button button_4 (.out(button_4_out));
  one_tick_pulse one_tick_pulse_1 (.A(button_1_out), .X(one_tick_pulse_1_x));
  one_tick_pulse one_tick_pulse_2 (.A(button_2_out), .X(one_tick_pulse_2_x));
  one_tick_pulse one_tick_pulse_3 (.A(button_3_out), .X(one_tick_pulse_3_x));
  one_tick_pulse one_tick_pulse_4 (.A(button_4_out), .X(one_tick_pulse_4_x));
  column_rgb column_rgb_5 (.C(state_memory_1_out_3_3));
  column_rgb column_rgb_6 (.C(state_memory_1_out_3_2));
  column_rgb column_rgb_7 (.C(state_memory_1_out_3));
  Button button_5 (.out(button_5_out));
  Button button_6 (.out(button_6_out));
  Button button_7 (.out(button_7_out));
  one_tick_pulse one_tick_pulse_5 (.A(button_5_out), .X(one_tick_pulse_5_x));
  one_tick_pulse one_tick_pulse_6 (.A(button_6_out), .X(one_tick_pulse_6_x));
  one_tick_pulse one_tick_pulse_7 (.A(button_7_out), .X(one_tick_pulse_7_x));
  turn_display Turn (.W(move_1_valid), .R(R_out), .P(Turn_p));
  buf buffer_1 (buffer_1_out, one_tick_pulse_7_x);
  buf buffer_2 (buffer_2_out, one_tick_pulse_6_x);
  buf buffer_3 (buffer_3_out, one_tick_pulse_5_x);
  buf buffer_4 (buffer_4_out, one_tick_pulse_4_x);
  buf buffer_5 (buffer_5_out, one_tick_pulse_3_x);
  buf buffer_6 (buffer_6_out, one_tick_pulse_2_x);
  buf buffer_7 (buffer_7_out, one_tick_pulse_1_x);
  nor nor_1 (nor_1_out, one_tick_pulse_7_x, one_tick_pulse_6_x, one_tick_pulse_5_x, one_tick_pulse_4_x, one_tick_pulse_3_x, one_tick_pulse_2_x, one_tick_pulse_1_x);
  Priority_Encoder priority_encoder_1 (
    .in0(buffer_1_out), .in1(buffer_2_out), .in2(buffer_3_out), .in3(buffer_4_out), .in4(buffer_5_out),
    .in5(buffer_6_out), .in6(buffer_7_out), .in7(nor_1_out), .out(priority_encoder_1_out), .en_in(1'b1));  // open: gs, en_out
  move move_1 (
    .P(Turn_p),
    .S({state_memory_1_out_3_7, state_memory_1_out_3_6, state_memory_1_out_3_5, state_memory_1_out_3_4, state_memory_1_out_3_3, state_memory_1_out_3_2, state_memory_1_out_3}),
    .C(priority_encoder_1_out), .S_new(move_1_s_new), .Valid(move_1_valid));
  reset_state reset_state_1 (.out_1(reset_state_1_out_1));
  Multiplexer #(.width(49)) multiplexer_1 (
    .in0(move_1_s_new), .in1(reset_state_1_out_1), .out(multiplexer_1_out), .sel(R_out));
  buf buffer_8 (buffer_8_out, or_1_out);
  or or_1 (or_1_out, move_1_valid, R_out);
  state_memory state_memory_1 (
    .in_1(multiplexer_1_out), .W(buffer_9_out),
    .out_3({state_memory_1_out_3_7, state_memory_1_out_3_6, state_memory_1_out_3_5, state_memory_1_out_3_4, state_memory_1_out_3_3, state_memory_1_out_3_2, state_memory_1_out_3}));
  buf buffer_9 (buffer_9_out, buffer_8_out);
endmodule

module color_decoder (
  input  [1:0] P,
  output G,
  output R,
  output B
);

  not not_1 (G, P[1]);
  nor nor_1 (B, P[1], P[0]);

  assign R = 1'b1;

  // Notes on the sheet:
  //   00 - empty
  //   10 - player 1
  //   01 - player 2
endmodule

module column_decoder (
  input  [6:0] C,
  output [1:0] R5,
  output [1:0] R4,
  output [1:0] R3,
  output [1:0] R2,
  output [1:0] R1,
  output [1:0] R0
);

  wire comparator_1_gt, comparator_2_gt, comparator_3_gt, comparator_4_gt, comparator_5_gt, comparator_6_gt,
       not_1_out, not_2_out, not_3_out, not_4_out, not_5_out, not_6_out;
  wire [2:0] priority_encoder_1_out;

  Priority_Encoder priority_encoder_1 (
    .in0(C[0]), .in1(C[1]), .in2(C[2]), .in3(C[3]), .in4(C[4]), .in5(C[5]), .in6(C[6]), .in7(1'b0),
    .out(priority_encoder_1_out), .en_in(1'b1));  // open: gs, en_out
  Comparator #(.mode("unsigned"), .width(3)) comparator_1 (
    .a(priority_encoder_1_out), .b(3'b101), .gt(comparator_1_gt));  // open: eq, lt
  Comparator #(.mode("unsigned"), .width(3)) comparator_2 (
    .a(priority_encoder_1_out), .b(3'b100), .gt(comparator_2_gt));  // open: eq, lt
  Comparator #(.mode("unsigned"), .width(3)) comparator_3 (
    .a(priority_encoder_1_out), .b(3'b011), .gt(comparator_3_gt));  // open: eq, lt
  Comparator #(.mode("unsigned"), .width(3)) comparator_4 (
    .a(priority_encoder_1_out), .b(3'b010), .gt(comparator_4_gt));  // open: eq, lt
  Comparator #(.mode("unsigned"), .width(3)) comparator_5 (
    .a(priority_encoder_1_out), .b(3'b001), .gt(comparator_5_gt));  // open: eq, lt
  Comparator #(.mode("unsigned"), .width(3)) comparator_6 (
    .a(priority_encoder_1_out), .b(3'b000), .gt(comparator_6_gt));  // open: eq, lt
  not not_1 (not_1_out, C[5]);
  not not_2 (not_2_out, C[4]);
  not not_3 (not_3_out, C[3]);
  not not_4 (not_4_out, C[2]);
  not not_5 (not_5_out, C[1]);
  not not_6 (not_6_out, C[0]);
  and and_1 (R5[0], not_1_out, comparator_1_gt);
  and and_2 (R5[1], C[5], comparator_1_gt);
  and and_3 (R4[0], not_2_out, comparator_2_gt);
  and and_4 (R4[1], C[4], comparator_2_gt);
  and and_5 (R3[0], not_3_out, comparator_3_gt);
  and and_6 (R3[1], C[3], comparator_3_gt);
  and and_7 (R2[0], not_4_out, comparator_4_gt);
  and and_8 (R2[1], C[2], comparator_4_gt);
  and and_9 (R1[0], not_5_out, comparator_5_gt);
  and and_10 (R1[1], C[1], comparator_5_gt);
  and and_11 (R0[0], not_6_out, comparator_6_gt);
  and and_12 (R0[1], C[0], comparator_6_gt);
endmodule

module column_rgb (
  input  [6:0] C
);

  wire [1:0] column_decoder_1_r0, column_decoder_1_r1, column_decoder_1_r2, column_decoder_1_r3,
       column_decoder_1_r4, column_decoder_1_r5;

  column_decoder column_decoder_1 (
    .C(C), .R5(column_decoder_1_r5), .R4(column_decoder_1_r4), .R3(column_decoder_1_r3),
    .R2(column_decoder_1_r2), .R1(column_decoder_1_r1), .R0(column_decoder_1_r0));
  color_decoder color_decoder_1 (.P(column_decoder_1_r5));  // open: G, R, B
  color_decoder color_decoder_2 (.P(column_decoder_1_r4));  // open: G, R, B
  color_decoder color_decoder_3 (.P(column_decoder_1_r3));  // open: G, R, B
  color_decoder color_decoder_4 (.P(column_decoder_1_r2));  // open: G, R, B
  color_decoder color_decoder_5 (.P(column_decoder_1_r1));  // open: G, R, B
  color_decoder color_decoder_6 (.P(column_decoder_1_r0));  // open: G, R, B
  // RGBLED rgbled_1: pin names not known
  // RGBLED rgbled_2: pin names not known
  // RGBLED rgbled_3: pin names not known
  // RGBLED rgbled_4: pin names not known
  // RGBLED rgbled_5: pin names not known
  // RGBLED rgbled_6: pin names not known
endmodule

module move_helper (
  input  P,
  input  [6:0] C,
  input  E,
  output Valid,
  output [6:0] C_new
);

  wire and_1_out, and_2_out, and_3_out, and_4_out, and_5_out, and_6_out, and_7_out, and_8_out, and_9_out,
       and_10_out, and_11_out, and_12_out, and_13_out, and_14_out, and_15_out, and_16_out, and_17_out,
       and_18_out, and_19_out, and_20_out, and_21_out, and_22_out, and_23_out, and_24_out, and_25_out,
       and_26_out, buffer_1_out, comparator_1_eq, comparator_1_gt, comparator_2_eq, comparator_2_gt,
       comparator_3_eq, comparator_3_gt, comparator_4_eq, comparator_4_gt, comparator_5_eq, comparator_5_gt,
       comparator_6_eq, comparator_6_gt, not_1_out, or_1_out, or_2_out, or_3_out, or_4_out, or_5_out,
       or_6_out, or_7_out;
  wire [2:0] priority_encoder_1_out;

  Priority_Encoder priority_encoder_1 (
    .in0(C[0]), .in1(C[1]), .in2(C[2]), .in3(C[3]), .in4(C[4]), .in5(C[5]), .in6(C[6]), .in7(1'b0),
    .out(priority_encoder_1_out), .en_in(1'b1));  // open: gs, en_out
  Comparator #(.mode("unsigned"), .width(3)) comparator_1 (
    .a(priority_encoder_1_out), .b(3'b101), .gt(comparator_1_gt), .eq(comparator_1_eq));  // open: lt
  Comparator #(.mode("unsigned"), .width(3)) comparator_2 (
    .a(priority_encoder_1_out), .b(3'b100), .gt(comparator_2_gt), .eq(comparator_2_eq));  // open: lt
  Comparator #(.mode("unsigned"), .width(3)) comparator_3 (
    .a(priority_encoder_1_out), .b(3'b011), .gt(comparator_3_gt), .eq(comparator_3_eq));  // open: lt
  Comparator #(.mode("unsigned"), .width(3)) comparator_4 (
    .a(priority_encoder_1_out), .b(3'b010), .gt(comparator_4_gt), .eq(comparator_4_eq));  // open: lt
  Comparator #(.mode("unsigned"), .width(3)) comparator_5 (
    .a(priority_encoder_1_out), .b(3'b001), .gt(comparator_5_gt), .eq(comparator_5_eq));  // open: lt
  Comparator #(.mode("unsigned"), .width(3)) comparator_6 (
    .a(priority_encoder_1_out), .b(3'b000), .gt(comparator_6_gt), .eq(comparator_6_eq));  // open: lt
  and and_1 (and_1_out, C[5], comparator_1_gt);
  and and_2 (and_2_out, C[4], comparator_2_gt);
  and and_3 (and_3_out, C[3], comparator_3_gt);
  and and_4 (and_4_out, C[2], comparator_4_gt);
  and and_5 (and_5_out, C[1], comparator_5_gt);
  and and_6 (and_6_out, C[0], comparator_6_gt);
  and and_7 (and_7_out, P, comparator_1_eq);
  and and_8 (and_8_out, P, comparator_2_eq);
  and and_9 (and_9_out, P, comparator_3_eq);
  and and_10 (and_10_out, P, comparator_4_eq);
  and and_11 (and_11_out, P, comparator_5_eq);
  and and_12 (and_12_out, P, comparator_6_eq);
  buf buffer_1 (buffer_1_out, E);
  not not_1 (not_1_out, E);
  or or_1 (or_1_out, C[6], comparator_1_eq);
  or or_2 (or_2_out, and_7_out, comparator_2_eq, and_1_out);
  or or_3 (or_3_out, and_8_out, comparator_3_eq, and_2_out);
  or or_4 (or_4_out, and_9_out, comparator_4_eq, and_3_out);
  or or_5 (or_5_out, and_10_out, comparator_5_eq, and_4_out);
  or or_6 (or_6_out, and_11_out, comparator_6_eq, and_5_out);
  or or_7 (or_7_out, and_12_out, and_6_out);
  nand nand_1 (Valid, C[6], buffer_1_out);
  and and_13 (and_13_out, or_1_out, buffer_1_out);
  and and_14 (and_14_out, C[6], not_1_out);
  and and_15 (and_15_out, or_2_out, buffer_1_out);
  and and_16 (and_16_out, C[5], not_1_out);
  and and_17 (and_17_out, or_3_out, buffer_1_out);
  and and_18 (and_18_out, C[4], not_1_out);
  and and_19 (and_19_out, or_4_out, buffer_1_out);
  and and_20 (and_20_out, C[3], not_1_out);
  and and_21 (and_21_out, or_5_out, buffer_1_out);
  and and_22 (and_22_out, C[2], not_1_out);
  and and_23 (and_23_out, or_6_out, buffer_1_out);
  and and_24 (and_24_out, C[1], not_1_out);
  and and_25 (and_25_out, or_7_out, buffer_1_out);
  and and_26 (and_26_out, C[0], not_1_out);
  or or_8 (C_new[6], and_13_out, and_14_out);
  or or_9 (C_new[5], and_15_out, and_16_out);
  or or_10 (C_new[4], and_17_out, and_18_out);
  or or_11 (C_new[3], and_19_out, and_20_out);
  or or_12 (C_new[2], and_21_out, and_22_out);
  or or_13 (C_new[1], and_23_out, and_24_out);
  or or_14 (C_new[0], and_25_out, and_26_out);
endmodule

module move (
  input  P,
  input  [48:0] S,
  input  [2:0] C,
  output [48:0] S_new,
  output Valid
);

  wire buffer_1_out, buffer_2_out, buffer_3_out, decoder_1_out0, decoder_1_out1, decoder_1_out2,
       decoder_1_out3, decoder_1_out4, decoder_1_out5, decoder_1_out6, decoder_1_out7, not_1_out;
  wire [6:0] move_helper_1_valid;

  Decoder #(.select(3)) decoder_1 (
    .out0(decoder_1_out0), .out1(decoder_1_out1), .out2(decoder_1_out2), .out3(decoder_1_out3),
    .out4(decoder_1_out4), .out5(decoder_1_out5), .out6(decoder_1_out6), .out7(decoder_1_out7), .sel(C),
    .en(1'b1));
  not not_1 (not_1_out, decoder_1_out7);
  buf buffer_1 (buffer_1_out, not_1_out);
  buf buffer_2 (buffer_2_out, buffer_1_out);
  buf buffer_3 (buffer_3_out, buffer_2_out);
  move_helper move_helper_1 (
    .P(P), .C(S[48:42]), .E(decoder_1_out6), .Valid(move_helper_1_valid[0]), .C_new(S_new[48:42]));
  move_helper move_helper_2 (
    .P(P), .C(S[41:35]), .E(decoder_1_out5), .Valid(move_helper_1_valid[1]), .C_new(S_new[41:35]));
  move_helper move_helper_3 (
    .P(P), .C(S[34:28]), .E(decoder_1_out4), .Valid(move_helper_1_valid[2]), .C_new(S_new[34:28]));
  move_helper move_helper_4 (
    .P(P), .C(S[27:21]), .E(decoder_1_out3), .Valid(move_helper_1_valid[3]), .C_new(S_new[27:21]));
  move_helper move_helper_5 (
    .P(P), .C(S[20:14]), .E(decoder_1_out2), .Valid(move_helper_1_valid[4]), .C_new(S_new[20:14]));
  move_helper move_helper_6 (
    .P(P), .C(S[13:7]), .E(decoder_1_out1), .Valid(move_helper_1_valid[5]), .C_new(S_new[13:7]));
  move_helper move_helper_7 (.P(P), .C(S[6:0]), .E(decoder_1_out0), .Valid(move_helper_1_valid[6]), .C_new(S_new[6:0]));
  and and_1 (Valid, move_helper_1_valid[0], move_helper_1_valid[1], move_helper_1_valid[2], move_helper_1_valid[3], move_helper_1_valid[4], move_helper_1_valid[5], move_helper_1_valid[6], buffer_3_out);
endmodule

module state_memory (
  input  [48:0] in_1,
  input  W,
  output [48:0] out_3
);

  Register #(.width(49)) register_1 (.D(in_1), .en(1'b1), .clk(W), .Q(out_3), .clr(1'b0));
endmodule

module reset_state (
  output [48:0] out_1
);


  assign out_1 = 49'h40810204081;
endmodule

module one_tick_pulse (
  input  A,
  output X
);

  wire not_1_out;

  and and_1 (X, A, not_1_out);
  not not_1 (not_1_out, A);
endmodule

module turn_display (
  input  W,
  input  R,
  output P
);

  wire d_ff_1_qn;
  wire [0:0] not_1_out;

  D_Flip_Flop d_ff_1 (.D(d_ff_1_qn), .clk(W), .Q(P), .Qn(d_ff_1_qn), .preset(R), .reset(1'b0));
  color_decoder color_decoder_1 (.P({P, not_1_out[0]}));  // open: G, R, B
  not not_1 (not_1_out[0], P);
  // RGBLED rgbled_1: pin names not known
endmodule
